# Fritzing sketch RADAR TÜM KOMPONENTLERLE (saved by Fritzing 0.9.4)
breadboards: 1

parts:
  Parça1 = Arduino Uno (Rev3)
  HC-SR04_Sensor_1 = HC-SR04 Ultrasonic Distance Sensor
  J1 = Basic Servo

nets:
  N1: Parça1.D5_PWM, J1.pulse
  N2: Parça1.D6_PWM, HC-SR04_Sensor_1.ECHO
  N3: Parça1.D7, HC-SR04_Sensor_1.TRIG
  VCC: Parça1.5V, HC-SR04_Sensor_1.VCC, J1.vcc
  GND: Parça1.GND, HC-SR04_Sensor_1.GND, J1.gnd
