# Fritzing sketch RADAR= HC-SR04 +BREADBOARD (saved by Fritzing 0.9.4)
breadboards: 1

parts:
  Parça1 = Arduino Uno (Rev3)
  HC-SR04_Sensor_1 = HC-SR04 Ultrasonic Distance Sensor

nets:
  N1: Parça1.D6_PWM, HC-SR04_Sensor_1.ECHO
  N2: Parça1.D7, HC-SR04_Sensor_1.TRIG
  5V: Parça1.5V, HC-SR04_Sensor_1.VCC
  GND: Parça1.GND, HC-SR04_Sensor_1.GND
