# Fritzing sketch radar fritzing ultasonik sensör ile (saved by Fritzing 0.9.4)

parts:
  HC-SR04_Sensor_1 = HC-SR04 Ultrasonic Distance Sensor
  Parça1 = Arduino Uno (Rev3)

nets:
  VCC: HC-SR04_Sensor_1.VCC, Parça1.5V
  N1: HC-SR04_Sensor_1.TRIG, Parça1.D7
  N2: HC-SR04_Sensor_1.ECHO, Parça1.D6_PWM
  GND: HC-SR04_Sensor_1.GND, Parça1.GND
