# Fritzing sketch radar projesi breadboard+ servo (saved by Fritzing 0.9.4)
breadboards: 1

parts:
  J1 = Basic Servo
  Parça1 = Arduino Uno (Rev3)

nets:
  GND: J1.gnd, Parça1.GND
  VCC: J1.vcc, Parça1.5V
  N1: J1.pulse, Parça1.D5_PWM
