# Fritzing sketch radar projesi servo ile (saved by Fritzing 0.9.4)

parts:
  Parça1 = Arduino Uno (Rev3) - ICSP
  J1 = Basic Servo

nets:
  N1: Parça1.D5_PWM, J1.pulse
  5V: Parça1.5V, J1.vcc
  GND: Parça1.GND, J1.gnd
